# Fritzing sketch motorBoard_001 (saved by Fritzing 0.8.3b)
circuit board: 17.8365cm x 7.12328cm
breadboards: 1

parts:
  Part3 = EasyDriver_v44
  Part4 = Arduino Mega 2560 (Rev3)
  J1 = screw terminal, 4 pins
  J2 = screw terminal, 4 pins
  J3 = screw terminal, 4 pins
  J4 = female pin header, 2 pins [form="♀ (female)"]
  Part1 = EasyDriver_v44
  Part2 = EasyDriver_v44
  J5 = male pin header, 17 pins [form="♂ (male)"]  # not connected
  J6 = double row male pin header, 36 pins [form="♂ (male)"]  # not connected

nets:
  GND: Part3.GND, Part4.GND, J4.pin1, Part1.GND, Part2.GND
  N1: Part3.V+, J4.pin2, Part1.V+, Part2.V+
  N2: Part3.STEP, Part4.D34
  N3: Part3.OUT2A, J3.pin1
  N4: Part3.OUT2B, J3.pin2
  N5: Part3.OUT1A, J3.pin3
  N6: Part3.OUT1B, J3.pin4
  N7: Part4.D30, Part1.STEP
  N8: Part4.D32, Part2.STEP
  N9: J1.pin1, Part1.OUT2A
  N10: J1.pin2, Part1.OUT2B
  N11: J1.pin3, Part1.OUT1A
  N12: J1.pin4, Part1.OUT1B
  N13: J2.pin1, Part2.OUT2A
  N14: J2.pin2, Part2.OUT2B
  N15: J2.pin3, Part2.OUT1A
  N16: J2.pin4, Part2.OUT1B
